# Fritzing sketch circuit (saved by Fritzing 0.9.3b)

parts:
  MH-ET_Live_Minikit_for_ESP1 = MH-ET Live Minikit for ESP32
  Load_Cell1 = Load Cell - Red/white/black/green
  Bauteil1 = HX711 Weighing Sensor Module
  S1 = Pushbutton [package="[THT]"]

nets:
  GND: MH-ET_Live_Minikit_for_ESP1.GND, Bauteil1.GND, S1.Pin_3, S1.Pin_4
  N1: MH-ET_Live_Minikit_for_ESP1.IO5, Bauteil1.CK/TX
  N2: MH-ET_Live_Minikit_for_ESP1.IO21, S1.Pin_1, S1.Pin_2
  N3: MH-ET_Live_Minikit_for_ESP1.IO16, Bauteil1.DO/RX
  VCC: MH-ET_Live_Minikit_for_ESP1.VCC, Bauteil1.VCC
  N4: Load_Cell1.wire1, Bauteil1.E+
  N5: Load_Cell1.wire2, Bauteil1.A-
  N6: Load_Cell1.wire3, Bauteil1.E-
  N7: Load_Cell1.wire4, Bauteil1.A+

custom parts:
  MH-ET Live Minikit for ESP32: MH-ET Live Minikit for ESP32 ( http://mh.nodebb.com/topic/8/mh-et-live-minikit-for-esp32/2/) PCB footprint is invalid.
  Load Cell - Red/white/black/green: A rectangle load cell/weighting pressure Sensor with four wires - Red, white, black, green. Normally corresponding with E+, E-, A+, A- respectively.
