# Fritzing sketch circuit (saved by Fritzing 0.9.3b)

parts:
  MH-ET_Live_Minikit_for_ESP1 = MH-ET Live Minikit for ESP32
  hc-sr1 = hc-sr04
  S1 = Momentary Switch [package=ksa_sealed_tac_switch]

nets:
  GND: MH-ET_Live_Minikit_for_ESP1.GND, hc-sr1.GND, S1.4
  N1: MH-ET_Live_Minikit_for_ESP1.IO17, hc-sr1.Trig
  N2: MH-ET_Live_Minikit_for_ESP1.IO16, hc-sr1.Echo
  VCC: MH-ET_Live_Minikit_for_ESP1.VCC, hc-sr1.VCC
  N3: MH-ET_Live_Minikit_for_ESP1.IO2, S1.1

custom parts:
  MH-ET Live Minikit for ESP32: MH-ET Live Minikit for ESP32 ( http://mh.nodebb.com/topic/8/mh-et-live-minikit-for-esp32/2/) PCB footprint is invalid.
