# Fritzing sketch Force (saved by Fritzing 1.0.5)

parts:
  Load_Cell1 = Load Cell - Red/white/black/green
  MCU1 = Wemos Lolin32lite
  U1 = LIPO-110mAh [package=lipo-110]
  S1 = Toggle Switch [package=THT]
  S2 = Pushbutton [package="[SMD]"]
  Bauteil1 = HX711 Weighing Sensor Module

nets:
  N1: Load_Cell1.wire1, Bauteil1.E+
  N2: Load_Cell1.wire2, Bauteil1.A+
  N3: Load_Cell1.wire3, Bauteil1.E-
  N4: Load_Cell1.wire4, Bauteil1.A-
  N5: MCU1.pin_13, Bauteil1.GND
  N6: MCU1.pin_14, S1.L2
  N7: MCU1.pin_18, S2.Pin_3, S2.Pin_4
  N8: MCU1.pin_20, Bauteil1.DO/RX
  N9: MCU1.pin_23, Bauteil1.CK/TX
  N10: MCU1.pin_28, Bauteil1.VCC
  N11: U1.+, S1.COM

notes:
  black - GND
  purple - DT
  brown - SCX
  red - VCC
  red - E+
  black - E-
  white - A-
  green - A+s

custom parts:
  Load Cell - Red/white/black/green: A rectangle load cell/weighting pressure Sensor with four wires - Red, white, black, green. Normally corresponding with E+, E-, A+, A- respectively.
  Wemos Lolin32lite: Wemos Lolinlite32 wifi and blue tooth board based on the ESP-32 cpu, digital I/Os 19, analog inputs 6, clock 240mhz, Flash 4Mbytes, lipo battery charger (500ma connection broken out on breadboard but not pcb), usb.
