# Fritzing sketch circuit (saved by Fritzing 0.9.3b)

parts:
  MH-ET_Live_Minikit_for_ESP1 = MH-ET Live Minikit for ESP32
  Bauteil1 = GY-VL53L0XV2 Laser Ranger Module
  S1 = Round Pushbutton

nets:
  GND: MH-ET_Live_Minikit_for_ESP1.GND, Bauteil1.GND, S1.leg1
  3.3V: MH-ET_Live_Minikit_for_ESP1.3.3V, Bauteil1.VCC
  N1: MH-ET_Live_Minikit_for_ESP1.IO22, Bauteil1.SCL
  N2: MH-ET_Live_Minikit_for_ESP1.IO21, Bauteil1.SDA
  N3: MH-ET_Live_Minikit_for_ESP1.IO27, S1.leg0

custom parts:
  MH-ET Live Minikit for ESP32: MH-ET Live Minikit for ESP32 ( http://mh.nodebb.com/topic/8/mh-et-live-minikit-for-esp32/2/) PCB footprint is invalid.
  GY-VL53L0XV2 Laser Ranger Module: The GY-VL53L0XV2 is based on the VL53L0X from ST Microelectronics, a time-of-flight ranging system integrated into a compact module.
