# Fritzing sketch vl53l0x (saved by Fritzing 1.0.2b)

parts:
  MCU1 = Wemos Lolin32lite
  Bauteil1 = GY-VL53L0XV2 Laser Ranger Module
  S1 = Pushbutton [package="[SMD]"]
  U1 = LIPO-110mAh [package=lipo-110]
  U2 = SWITCH_SPDT [package=kps-1290]
  R1 = Resistor [tolerance=±5% resistance=1k package="2010 [SMD]"]
  R2 = Resistor [tolerance=±5% resistance=1k package="2010 [SMD]"]

nets:
  N1: MCU1.pin_4, MCU1.pin_13, Bauteil1.GND, S1.Pin_3, S1.Pin_4, U1.-, R1.Pin_1
  N2: MCU1.pin_8, R1.Pin_0, R2.Pin_1
  N3: MCU1.pin_10, S1.Pin_1, S1.Pin_2
  N4: MCU1.pin_11, Bauteil1.SDA
  N5: MCU1.pin_12, Bauteil1.SCL
  N6: MCU1.pin_14, U2.S
  N7: MCU1.pin_28, Bauteil1.VCC
  N8: U1.+, U2.P

custom parts:
  Wemos Lolin32lite: Wemos Lolinlite32 wifi and blue tooth board based on the ESP-32 cpu, digital I/Os 19, analog inputs 6, clock 240mhz, Flash 4Mbytes, lipo battery charger (500ma connection broken out on breadboard but not pcb), usb.
  GY-VL53L0XV2 Laser Ranger Module: The GY-VL53L0XV2 is based on the VL53L0X from ST Microelectronics, a time-of-flight ranging system integrated into a compact module.
