# Fritzing sketch light barrier (saved by Fritzing 0.9.3b)
breadboards: 1

parts:
  Q1 = NPN-Transistor [package="TO92 [THT]"]
  R1 = Resistor [tolerance=±5% resistance=220 package=THT]
  R2 = Resistor [tolerance=±5% resistance=100k package=THT]
  D1 = LTE-302 [package=lte-302]  # not connected
  LED1 = LED - 3mm [color="Red (633nm)" package="3 mm [THT]"]
  R3 = Resistor [tolerance=±5% resistance=10 package=THT]
  Q2 = LTR-301 [package=ltr-301]  # not connected
  MH-ET_Live_Minikit_for_ESP1 = MH-ET Live Minikit for ESP32

nets:
  N1: Q1.E, LED1.anode
  N2: Q1.B, R2.Pin_0, MH-ET_Live_Minikit_for_ESP1.SVN
  N3: R1.Pin_1, R2.Pin_1, R3.Pin_1, MH-ET_Live_Minikit_for_ESP1.3.3V

custom parts:
  MH-ET Live Minikit for ESP32: MH-ET Live Minikit for ESP32 ( http://mh.nodebb.com/topic/8/mh-et-live-minikit-for-esp32/2/) PCB footprint is invalid.
