# Fritzing sketch BREAK_BEAM_Receiver_OLED (saved by Fritzing 1.0.8)

parts:
  MCU2 = Wemos Lolin32lite
  LiPo-Batterie1 = LIPO-110mAh [package=lipo-110]
  U2 = SWITCH_SPDT [package=kps-1290]
  S1 = 0.91 inch OLED I2C Display 128 x 32 Pixels
  M1 = IR break beam 3mm rx [package=THT]
  M2 = IR break beam 3mm tx [package=THT]
  Bauteil1 = LilyPad Coin Cell Battery Holder
  U3 = SWITCH_SPDT [package=kps-1290]
  R1 = Resistor [tolerance=±5% resistance=100 package="2512 [SMD]"]
  R2 = Resistor [tolerance=±5% resistance=100 package="2512 [SMD]"]
  LED1 = LED - 5mm [color="Red (635nm)" current=0.030A package="5 mm [THT]"]
  LED2 = LED - 5mm [color="Red (635nm)" current=0.030A package="5 mm [THT]"]
  S2 = Pushbutton [package="[THT]"]

nets:
  N1: MCU2.pin_6, R1.Pin_0
  N2: MCU2.pin_9, M1.pin2, LED1.cathode
  N3: MCU2.pin_10, S2.Pin_3, S2.Pin_4
  N4: MCU2.pin_13, S1.GND, M1.pin3, S2.Pin_1, S2.Pin_2
  N5: MCU2.pin_14, U2.P
  N6: MCU2.pin_15, LiPo-Batterie1.-
  N7: MCU2.pin_21, S1.SDA
  N8: MCU2.pin_22, S1.SCL
  N9: MCU2.pin_28, S1.VCC, M1.pin1
  N10: LiPo-Batterie1.+, U2.O
  N11: M2.pin1, U3.P, R2.Pin_0
  N12: M2.pin2, Bauteil1.+, U3.O, LED2.cathode

custom parts:
  Wemos Lolin32lite: Wemos Lolinlite32 wifi and blue tooth board based on the ESP-32 cpu, digital I/Os 19, analog inputs 6, clock 240mhz, Flash 4Mbytes, lipo battery charger (500ma connection broken out on breadboard but not pcb), usb.
  IR break beam 3mm rx: Infrared break beam Sensor rx module.
  IR break beam 3mm tx: Infrared break beam Sensor tx module.
