# Fritzing sketch LightGate (saved by Fritzing 1.0.2b)

parts:
  MCU1 = Wemos Lolin32lite
  Enc1 = shaft encoder
  U1 = RJ45 Jack [package=rj45-8]
  U2 = RJ45 Jack [package=rj45-8]
  Enc2 = shaft encoder
  U3 = LIPO-110mAh [package=lipo-110]
  U4 = SWITCH_SPDT [package=kps-1290]
  LED1 = smd LED [color="Red (633nm)" package="1206 [SMD]"]
  LED2 = smd LED [color="Red (633nm)" package="1206 [SMD]"]
  R1 = Resistor [tolerance=±5% resistance=220 package="0603 [SMD]"]
  R2 = Resistor [tolerance=±5% resistance=220 package="0603 [SMD]"]
  IR-LED1 = IRE [package="1206 [SMD]"]  # not connected
  Q2 = LTR-301 [package=ltr-301]  # not connected
  IR-LED2 = IRE [package="1206 [SMD]"]  # not connected
  Q3 = LTR-301 [package=ltr-301]  # not connected

nets:
  N1: MCU1.pin_8, U1.4
  N2: MCU1.pin_13, Enc1.GND, U1.7, U3.-, LED2.cathode
  N3: MCU1.pin_14, U4.P
  N4: MCU1.pin_21, U1.3
  N5: MCU1.pin_22, Enc1.OUT, R1.Pin_1
  N6: MCU1.pin_28, Enc1.VCC, U1.2
  N7: U2.2, Enc2.VCC
  N8: U2.3, Enc2.OUT, R2.Pin_0
  N9: U2.4, U2.7, Enc2.GND, LED1.cathode
  N10: U3.+, U4.S

notes:
  second light gate
  first light gate
  for single light gate, rj45 not needed

custom parts:
  Wemos Lolin32lite: Wemos Lolinlite32 wifi and blue tooth board based on the ESP-32 cpu, digital I/Os 19, analog inputs 6, clock 240mhz, Flash 4Mbytes, lipo battery charger (500ma connection broken out on breadboard but not pcb), usb.
  IRE: IR Emitter Diode
  LTR-301: receiving IR phototransistor
