# Fritzing sketch LightGate_single (saved by Fritzing 0.9.6b)

parts:
  MCU1 = Wemos Lolin32lite
  Lichtschranke = shaft encoder
  LED = LED - 5mm [color="Red (633nm)" current=0.030A package="5 mm [THT]"]
  LiPo-Batterie = LIPO-110mAh [package=lipo-110]
  U1 = SWITCH_SPDT [package=kps-1290]

nets:
  N1: MCU1.pin_13, Lichtschranke.GND, LED.cathode
  N2: MCU1.pin_14, U1.P
  N3: MCU1.pin_15, LiPo-Batterie.-
  N4: MCU1.pin_16, LED.anode
  N5: MCU1.pin_22, Lichtschranke.OUT
  N6: MCU1.pin_28, Lichtschranke.VCC
  N7: LiPo-Batterie.+, U1.S

custom parts:
  Wemos Lolin32lite: Wemos Lolinlite32 wifi and blue tooth board based on the ESP-32 cpu, digital I/Os 19, analog inputs 6, clock 240mhz, Flash 4Mbytes, lipo battery charger (500ma connection broken out on breadboard but not pcb), usb.
