# Fritzing sketch Magnetometer - 90393 (saved by Fritzing 0.9.6b)

parts:
  MCU1 = Wemos Lolin32lite
  S1 = Pushbutton [package="[SMD]"]
  U1 = LIPO-110mAh [package=lipo-110]
  U2 = SWITCH_SPDT [package=kps-1290]
  Bauteil2 = Adafruit MLX90393 [part_number="Adafruit #4022"]

nets:
  N1: MCU1.pin_4, U1.-
  N2: MCU1.pin_10, S1.Pin_1, S1.Pin_2
  N3: MCU1.pin_11, Bauteil2.SDA
  N4: MCU1.pin_12, Bauteil2.SCL
  N5: MCU1.pin_13, S1.Pin_3, S1.Pin_4, Bauteil2.GND
  N6: MCU1.pin_14, U2.S
  N7: MCU1.pin_28, Bauteil2.VCC
  N8: U1.+, U2.P

custom parts:
  Wemos Lolin32lite: Wemos Lolinlite32 wifi and blue tooth board based on the ESP-32 cpu, digital I/Os 19, analog inputs 6, clock 240mhz, Flash 4Mbytes, lipo battery charger (500ma connection broken out on breadboard but not pcb), usb.
  Adafruit MLX90393: Measure the invisible magnetic fields that surround us, with this wide-range magnetometer. The MLX90393 is a wide range magnetic field sensor, that can measure 16-bits in ranges from ±5mT up to ±50mT in all 3 axes. Compared to most magnetometers, this gives a huge range, which makes it excellent for detecting magnets and magnetic orientation, rather than the Earth's magnetic field. (Magnets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
