# Fritzing sketch INA (saved by Fritzing 0.9.6b)

parts:
  INA1 = INA219 DC Current Sensor Breakout
  MCU1 = Wemos Lolin32lite
  J1 = top view banana jack blue [package=THT]
  J2 = top view banana jack red [package=THT]
  J3 = top view banana jack black [package=THT]
  U1 = LIPO-110mAh [package=lipo-110]
  U2 = SWITCH_SPDT [package=kps-1290]

nets:
  N1: INA1.VCC, MCU1.pin_28
  N2: INA1.GND, MCU1.pin_13, J3.pin1
  N3: INA1.SCL, MCU1.pin_16
  N4: INA1.SDA, MCU1.pin_17
  N5: INA1.Vin-, J1.pin1
  N6: INA1.Vin+, J2.pin1
  N7: MCU1.pin_14, U2.P
  N8: U1.+, U2.S

custom parts:
  INA219 DC Current Sensor Breakout: INA DC Current Sensor Breakout
  Wemos Lolin32lite: Wemos Lolinlite32 wifi and blue tooth board based on the ESP-32 cpu, digital I/Os 19, analog inputs 6, clock 240mhz, Flash 4Mbytes, lipo battery charger (500ma connection broken out on breadboard but not pcb), usb.
  top view banana jack blue: Top view banana jack blue.
  top view banana jack red: Top view banana jack red.
  top view banana jack black: Top view banana jack black.
